# Fritzing sketch sketch (saved by Fritzing 0.9.4)
breadboards: 1

parts:
  MH-Z1 = MH-Z14 [part_number=MH-Z14]
  OLED1 = OLED 128x64 I2C Monochrome Display
  M1 = DOIT Esp32 DevKit v1 (30 pins long, 11 pins width) [part_number=ESP32S-PIN30]

nets:
  N1: MH-Z1.1, MH-Z1.15, M1.VIN
  GND: MH-Z1.2, MH-Z1.3, OLED1.GND, M1.GND
  N2: MH-Z1.10, MH-Z1.13, M1.TX2
  N3: MH-Z1.11, MH-Z1.14, M1.RX2
  VDD: OLED1.VDD, M1.3V3
  N4: OLED1.SCK, M1.D22
  N5: OLED1.SDA, M1.D21

custom parts:
  MH-Z14: MH-Z14 NDIR Infrared gas module is a common type, small size sensor, using non-dispersive infrared (NDIR) principle to detect the existence of CO2 in the air, with good selectivity, non-oxygen dependant, long life. Built-in temperature sensor can do temperature compensation; and it has digital output and analog voltage output.
  DOIT Esp32 DevKit v1 (30 pins long, 11 pins width): The DOIT Esp32 DevKit v1 is one of the development board created by DOIT to evaluate the ESP-WROOM-32 module. It is based on the ESP32 microcontroller that boasts Wifi, Bluetooth, Ethernet and Low Power support all in a single chip. (vanepp) made breadboard work, adjusted pin numbering and labels and reduced size of schematic and cleaned up pcb. This chip is 30pins long (2 x15) and 11 pins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
